# Fritzing sketch esquema (saved by Fritzing 0.7.7b)
breadboards: 1

parts:
  Arduino1 = Arduino
  LED1 = LED - 5mm [color="Red (633nm)" package="5 mm [THT]"]
  R1 = Resistor [tolerance=±5% resistance=220 package=THT]
  LED2 = LED - 5mm [color="Red (633nm)" package="5 mm [THT]"]
  LED3 = LED - 5mm [color="Red (633nm)" package="5 mm [THT]"]
  LED4 = LED - 5mm [color="Red (633nm)" package="5 mm [THT]"]
  R2 = Resistor [tolerance=±5% resistance=220 package=THT]
  R3 = Resistor [tolerance=±5% resistance=220 package=THT]
  R4 = Resistor [tolerance=±5% resistance=220 package=THT]
  S1 = Pushbutton [package="[THT]"]
  S2 = Pushbutton [package="[THT]"]
  S3 = Pushbutton [package="[THT]"]
  S4 = Pushbutton [package="[THT]"]
  R5 = Resistor [tolerance=±5% resistance=220 package=THT]
  R6 = Resistor [tolerance=±5% resistance=220 package=THT]
  R7 = Resistor [tolerance=±5% resistance=220 package=THT]
  R8 = Resistor [tolerance=±5% resistance=220 package=THT]
  J1 = Piezo Speaker
  R9 = Resistor [tolerance=±5% resistance=220 package=THT]

nets:
  N1: Arduino1.GND, R1.Pin_0, R2.Pin_0, R3.Pin_0, R4.Pin_0, R5.Pin_1, R6.Pin_1, R7.Pin_1, R8.Pin_1, J1.pin1
  N2: Arduino1.D12, LED4.anode
  N3: Arduino1.D11, LED3.anode
  N4: Arduino1.D10, LED2.anode
  N5: Arduino1.D9, LED1.anode
  N6: Arduino1.D8, R9.Pin_1
  N7: Arduino1.D5, S4.Pin_3, S4.Pin_4
  N8: Arduino1.D4, S3.Pin_3, S3.Pin_4
  N9: Arduino1.D3, S2.Pin_3, S2.Pin_4
  N10: Arduino1.D2, S1.Pin_3, S1.Pin_4
  N11: Arduino1.+5V, S1.Pin_1, S1.Pin_2, S2.Pin_1, S2.Pin_2, S3.Pin_1, S3.Pin_2, S4.Pin_1, S4.Pin_2, R5.Pin_0, R6.Pin_0, R7.Pin_0, R8.Pin_0
  N12: LED1.cathode, R1.Pin_1
  N13: LED2.cathode, R2.Pin_1
  N14: LED3.cathode, R3.Pin_1
  N15: LED4.cathode, R4.Pin_1
  N16: J1.pin2, R9.Pin_0
